// Logisim project RV32I_Single_Cycle_CPU.circ as structural Verilog: 14 circuits, main circuit main
module main (
);

  wire branch_selector_1_o_p, CLK_out, control_unit_1_branch, control_unit_1_load, control_unit_1_store,
       IM_to_Reg, Operand_B_Selector, RESET_out;
  wire [1:0] Immediate_Selector, Next_PC_Selector, Operand_A_Selector;
  wire [3:0] ALU_Operations_Selector;
  wire [31:0] adder_2_out, alu_1_data_memory, DM_to_Reg, I, immediate_generator_1_s_type,
       immediate_generator_1_u_type, multiplexer_1_out, multiplexer_2_out, multiplexer_3_out,
       multiplexer_4_out, multiplexer_5_out, PC, PC_4, ram_1_data, register_file_1_source_register_1_2,
       register_file_1_source_register_2_2, rom_1_data, SB, UJ;

  Clock CLK (.out(CLK_out));
  Register #(.width(32)) register_1 (.D(multiplexer_1_out), .Q(PC), .clk(CLK_out), .clr(RESET_out));  // open: en
  Button RESET (.out(RESET_out));
  Multiplexer #(.select(2), .width(32), .enable("false")) multiplexer_1 (
    .in0(PC_4), .in1(adder_2_out), .in2(multiplexer_2_out), .in3(UJ), .out(multiplexer_1_out),
    .sel(Next_PC_Selector));
  Branch_Selector branch_selector_1 (
    .func_3(rom_1_data[14:12]), .rs1(register_file_1_source_register_1_2),
    .rs2(register_file_1_source_register_2_2), .EN(control_unit_1_branch), .O_P(branch_selector_1_o_p));
  Adder #(.width(32)) adder_1 (.a(PC), .b(32'h4), .out(PC_4));  // open: cin, cout
  Multiplexer #(.width(32), .enable("false")) multiplexer_2 (
    .in0(PC_4), .in1(SB), .out(multiplexer_2_out), .sel(branch_selector_1_o_p));
  ROM #(.addrWidth(12), .dataWidth(32)) rom_1 (.addr(PC[13:2]), .data(rom_1_data));  // open: sel
  Control_Unit control_unit_1 (
    .Instruction_Memory(rom_1_data[6:0]), .Write(IM_to_Reg), .Store(control_unit_1_store),
    .Load(control_unit_1_load), .Branch(control_unit_1_branch), .Operand_A(Operand_A_Selector),
    .Operand_B(Operand_B_Selector), .Immediate_Selector(Immediate_Selector), .Next_PC(Next_PC_Selector),
    .ALU_Operators(ALU_Operations_Selector), .func_7(rom_1_data[30]), .func_3(rom_1_data[14:12]));
  Immediate_Generator immediate_generator_1 (
    .Instruction_Memory(rom_1_data), .I_Type(I), .S_Type(immediate_generator_1_s_type), .SB_Type(SB),
    .U_Type(immediate_generator_1_u_type), .UJ_Type(UJ), .PC(PC));
  Register_File register_file_1 (
    .Instruction_Memory(DM_to_Reg), .Source_Register_2_2(register_file_1_source_register_2_2),
    .EN(IM_to_Reg), .Destination_Register(rom_1_data[11:7]), .Source_Register_2(rom_1_data[24:20]),
    .Source_Register_1_2(register_file_1_source_register_1_2), .Source_Register_1(rom_1_data[19:15]),
    .CLK(CLK_out));
  Multiplexer #(.select(2), .width(32), .enable("false")) multiplexer_3 (
    .in0(I), .in1(immediate_generator_1_u_type), .in2(immediate_generator_1_s_type), .out(multiplexer_3_out),
    .sel(Immediate_Selector));  // open: in3
  Adder #(.width(32)) adder_2 (.a(I), .b(register_file_1_source_register_1_2), .out(adder_2_out));  // open: cin, cout
  Multiplexer #(.select(2), .width(32), .enable("false")) multiplexer_4 (
    .in0(register_file_1_source_register_1_2), .in1(PC_4), .in2(PC), .in3({32{1'b0}}),
    .out(multiplexer_4_out), .sel(Operand_A_Selector));
  Multiplexer #(.width(32), .enable("false")) multiplexer_5 (
    .in0(register_file_1_source_register_2_2), .in1(multiplexer_3_out), .out(multiplexer_5_out),
    .sel(Operand_B_Selector));
  ALU alu_1 (
    .Operation_Select(ALU_Operations_Selector), .Data_Memory(alu_1_data_memory),
    .Operand_A(multiplexer_4_out), .Operand_B(multiplexer_5_out));
  RAM #(.addrWidth(12), .dataWidth(32), .bus("separate")) ram_1 (
    .addr(alu_1_data_memory[13:2]), .din(register_file_1_source_register_2_2), .data(ram_1_data),
    .str(control_unit_1_store), .clk(CLK_out), .ld(control_unit_1_load));  // open: sel, clr
  Multiplexer #(.width(32), .enable("false")) multiplexer_6 (
    .in0(alu_1_data_memory), .in1(ram_1_data), .out(DM_to_Reg), .sel(control_unit_1_load));

  // Notes on the sheet:
  //   Made By
  //   Ammar Bin Amir
  //   contents of rom_1 (hex, n*v repeats v):
  //   293 128293 502023 2303 ff5ff0ef
  //   RV32I Single Cycle
endmodule

module Type_Decoder (
  input  [6:0] Instruction_Memory,
  output R_Type,
  output I_Type,
  output I_Type_2,
  output I_Type_3,
  output S_Type,
  output SB_Type,
  output U_Type,
  output U_Type_2,
  output UJ_Type
);

  Comparator #(.width(7)) comparator_1 (.a(Instruction_Memory), .b(7'b0110011), .eq(R_Type));  // open: gt, lt
  Comparator #(.width(7)) comparator_2 (.a(Instruction_Memory), .b(7'b0000011), .eq(I_Type));  // open: gt, lt
  Comparator #(.width(7)) comparator_3 (.a(Instruction_Memory), .b(7'b0010011), .eq(I_Type_2));  // open: gt, lt
  Comparator #(.width(7)) comparator_4 (.a(Instruction_Memory), .b(7'b1100111), .eq(I_Type_3));  // open: gt, lt
  Comparator #(.width(7)) comparator_5 (.a(Instruction_Memory), .b(7'b0100011), .eq(S_Type));  // open: gt, lt
  Comparator #(.width(7)) comparator_6 (.a(Instruction_Memory), .b(7'b1100011), .eq(SB_Type));  // open: gt, lt
  Comparator #(.width(7)) comparator_7 (.a(Instruction_Memory), .b(7'b0010111), .eq(U_Type));  // open: gt, lt
  Comparator #(.width(7)) comparator_8 (.a(Instruction_Memory), .b(7'b0110111), .eq(U_Type_2));  // open: gt, lt
  Comparator #(.width(7)) comparator_9 (.a(Instruction_Memory), .b(7'b1101111), .eq(UJ_Type));  // open: gt, lt
endmodule

module Immediate_Generator (
  input  [31:0] Instruction_Memory,
  input  [31:0] PC,
  output [31:0] I_Type,
  output [31:0] S_Type,
  output [31:0] SB_Type,
  output [31:0] U_Type,
  output [31:0] UJ_Type
);

  wire [31:0] bit_extender_1_out, bit_extender_4_out, bit_extender_5_out;

  assign bit_extender_1_out = {{12{Instruction_Memory[31]}}, Instruction_Memory[31:12]};  // Bit_Extender bit_extender_1
  assign I_Type = {{20{Instruction_Memory[31]}}, Instruction_Memory[31:20]};  // Bit_Extender bit_extender_2
  assign S_Type = {{20{Instruction_Memory[31]}}, {Instruction_Memory[31:25], Instruction_Memory[11:7]}};  // Bit_Extender bit_extender_3
  assign bit_extender_4_out = {{19{Instruction_Memory[31]}}, {Instruction_Memory[31], Instruction_Memory[7], Instruction_Memory[30:25], Instruction_Memory[11:8], 1'b0}};  // Bit_Extender bit_extender_4
  assign bit_extender_5_out = {{11{Instruction_Memory[31]}}, {Instruction_Memory[31], Instruction_Memory[19:12], Instruction_Memory[20], Instruction_Memory[30:21], 1'b0}};  // Bit_Extender bit_extender_5
  Adder #(.width(32)) adder_1 (.a(bit_extender_4_out), .b(PC), .out(SB_Type));  // open: cin, cout
  Shifter #(.width(32)) shifter_1 (.in(bit_extender_1_out), .\dist (5'b01100), .out(U_Type));
  Adder #(.width(32)) adder_2 (.a(bit_extender_5_out), .b(PC), .out(UJ_Type));  // open: cin, cout
endmodule

module Register_File (
  input  [31:0] Instruction_Memory,
  input  EN,
  input  [4:0] Destination_Register,
  input  [4:0] Source_Register_1,
  input  [4:0] Source_Register_2,
  input  CLK,
  output [31:0] Source_Register_1_2,
  output [31:0] Source_Register_2_2
);

  wire decoder_1_out1, decoder_1_out2, decoder_1_out3, decoder_1_out4, decoder_1_out5, decoder_1_out6,
       decoder_1_out7, decoder_1_out8, decoder_1_out9, decoder_1_out10, decoder_1_out11, decoder_1_out12,
       decoder_1_out13, decoder_1_out14, decoder_1_out15, decoder_1_out16, decoder_1_out17, decoder_1_out18,
       decoder_1_out19, decoder_1_out20, decoder_1_out21, decoder_1_out22, decoder_1_out23, decoder_1_out24,
       decoder_1_out25, decoder_1_out26, decoder_1_out27, decoder_1_out28, decoder_1_out29, decoder_1_out30,
       decoder_1_out31;
  wire [31:0] register_1_q, register_2_q, register_3_q, register_4_q, register_5_q, register_6_q,
       register_7_q, register_8_q, register_9_q, register_10_q, register_11_q, register_12_q, register_13_q,
       register_14_q, register_15_q, register_16_q, register_17_q, register_18_q, register_19_q,
       register_20_q, register_21_q, register_22_q, register_23_q, register_24_q, register_25_q,
       register_26_q, register_27_q, register_28_q, register_29_q, register_30_q, register_31_q;

  Decoder #(.select(5), .disabled(0)) decoder_1 (
    .out1(decoder_1_out1), .out2(decoder_1_out2), .out3(decoder_1_out3), .out4(decoder_1_out4),
    .out5(decoder_1_out5), .out6(decoder_1_out6), .out7(decoder_1_out7), .out8(decoder_1_out8),
    .out9(decoder_1_out9), .out10(decoder_1_out10), .out11(decoder_1_out11), .out12(decoder_1_out12),
    .out13(decoder_1_out13), .out14(decoder_1_out14), .out15(decoder_1_out15), .out16(decoder_1_out16),
    .out17(decoder_1_out17), .out18(decoder_1_out18), .out19(decoder_1_out19), .out20(decoder_1_out20),
    .out21(decoder_1_out21), .out22(decoder_1_out22), .out23(decoder_1_out23), .out24(decoder_1_out24),
    .out25(decoder_1_out25), .out26(decoder_1_out26), .out27(decoder_1_out27), .out28(decoder_1_out28),
    .out29(decoder_1_out29), .out30(decoder_1_out30), .out31(decoder_1_out31), .sel(Destination_Register),
    .en(EN));  // open: out0
  Register #(.width(32)) register_1 (
    .D(Instruction_Memory), .en(decoder_1_out1), .Q(register_1_q), .clk(CLK));  // open: clr
  Register #(.width(32)) register_2 (
    .D(Instruction_Memory), .en(decoder_1_out2), .Q(register_2_q), .clk(CLK));  // open: clr
  Register #(.width(32)) register_3 (
    .D(Instruction_Memory), .en(decoder_1_out3), .Q(register_3_q), .clk(CLK));  // open: clr
  Register #(.width(32)) register_4 (
    .D(Instruction_Memory), .en(decoder_1_out4), .Q(register_4_q), .clk(CLK));  // open: clr
  Register #(.width(32)) register_5 (
    .D(Instruction_Memory), .en(decoder_1_out5), .Q(register_5_q), .clk(CLK));  // open: clr
  Register #(.width(32)) register_6 (
    .D(Instruction_Memory), .en(decoder_1_out6), .Q(register_6_q), .clk(CLK));  // open: clr
  Register #(.width(32)) register_7 (
    .D(Instruction_Memory), .en(decoder_1_out7), .Q(register_7_q), .clk(CLK));  // open: clr
  Register #(.width(32)) register_8 (
    .D(Instruction_Memory), .en(decoder_1_out8), .Q(register_8_q), .clk(CLK));  // open: clr
  Register #(.width(32)) register_9 (
    .D(Instruction_Memory), .en(decoder_1_out9), .Q(register_9_q), .clk(CLK));  // open: clr
  Register #(.width(32)) register_10 (
    .D(Instruction_Memory), .en(decoder_1_out10), .Q(register_10_q), .clk(CLK));  // open: clr
  Register #(.width(32)) register_11 (
    .D(Instruction_Memory), .en(decoder_1_out11), .Q(register_11_q), .clk(CLK));  // open: clr
  Register #(.width(32)) register_12 (
    .D(Instruction_Memory), .en(decoder_1_out12), .Q(register_12_q), .clk(CLK));  // open: clr
  Register #(.width(32)) register_13 (
    .D(Instruction_Memory), .en(decoder_1_out13), .Q(register_13_q), .clk(CLK));  // open: clr
  Register #(.width(32)) register_14 (
    .D(Instruction_Memory), .en(decoder_1_out14), .Q(register_14_q), .clk(CLK));  // open: clr
  Register #(.width(32)) register_15 (
    .D(Instruction_Memory), .en(decoder_1_out15), .Q(register_15_q), .clk(CLK));  // open: clr
  Register #(.width(32)) register_16 (
    .D(Instruction_Memory), .en(decoder_1_out16), .Q(register_16_q), .clk(CLK));  // open: clr
  Register #(.width(32)) register_17 (
    .D(Instruction_Memory), .en(decoder_1_out17), .Q(register_17_q), .clk(CLK));  // open: clr
  Register #(.width(32)) register_18 (
    .D(Instruction_Memory), .en(decoder_1_out18), .Q(register_18_q), .clk(CLK));  // open: clr
  Register #(.width(32)) register_19 (
    .D(Instruction_Memory), .en(decoder_1_out19), .Q(register_19_q), .clk(CLK));  // open: clr
  Register #(.width(32)) register_20 (
    .D(Instruction_Memory), .en(decoder_1_out20), .Q(register_20_q), .clk(CLK));  // open: clr
  Register #(.width(32)) register_21 (
    .D(Instruction_Memory), .en(decoder_1_out21), .Q(register_21_q), .clk(CLK));  // open: clr
  Register #(.width(32)) register_22 (
    .D(Instruction_Memory), .en(decoder_1_out22), .Q(register_22_q), .clk(CLK));  // open: clr
  Register #(.width(32)) register_23 (
    .D(Instruction_Memory), .en(decoder_1_out23), .Q(register_23_q), .clk(CLK));  // open: clr
  Register #(.width(32)) register_24 (
    .D(Instruction_Memory), .en(decoder_1_out24), .Q(register_24_q), .clk(CLK));  // open: clr
  Register #(.width(32)) register_25 (
    .D(Instruction_Memory), .en(decoder_1_out25), .Q(register_25_q), .clk(CLK));  // open: clr
  Register #(.width(32)) register_26 (
    .D(Instruction_Memory), .en(decoder_1_out26), .Q(register_26_q), .clk(CLK));  // open: clr
  Register #(.width(32)) register_27 (
    .D(Instruction_Memory), .en(decoder_1_out27), .Q(register_27_q), .clk(CLK));  // open: clr
  Register #(.width(32)) register_28 (
    .D(Instruction_Memory), .en(decoder_1_out28), .Q(register_28_q), .clk(CLK));  // open: clr
  Register #(.width(32)) register_29 (
    .D(Instruction_Memory), .en(decoder_1_out29), .Q(register_29_q), .clk(CLK));  // open: clr
  Register #(.width(32)) register_30 (
    .D(Instruction_Memory), .en(decoder_1_out30), .Q(register_30_q), .clk(CLK));  // open: clr
  Register #(.width(32)) register_31 (
    .D(Instruction_Memory), .en(decoder_1_out31), .Q(register_31_q), .clk(CLK));  // open: clr
  Multiplexer #(.select(5), .width(32), .enable("false")) multiplexer_1 (
    .in0({32{1'b0}}), .in1(register_1_q), .in2(register_2_q), .in3(register_3_q), .in4(register_4_q),
    .in5(register_5_q), .in6(register_6_q), .in7(register_7_q), .in8(register_8_q), .in9(register_9_q),
    .in10(register_10_q), .in11(register_11_q), .in12(register_12_q), .in13(register_13_q),
    .in14(register_14_q), .in15(register_15_q), .in16(register_16_q), .in17(register_17_q),
    .in18(register_18_q), .in19(register_19_q), .in20(register_20_q), .in21(register_21_q),
    .in22(register_22_q), .in23(register_23_q), .in24(register_24_q), .in25(register_25_q),
    .in26(register_26_q), .in27(register_27_q), .in28(register_28_q), .in29(register_29_q),
    .in30(register_30_q), .in31(register_31_q), .out(Source_Register_1_2), .sel(Source_Register_1));
  Multiplexer #(.select(5), .width(32), .enable("false")) multiplexer_2 (
    .in0({32{1'b0}}), .in1(register_1_q), .in2(register_2_q), .in3(register_3_q), .in4(register_4_q),
    .in5(register_5_q), .in6(register_6_q), .in7(register_7_q), .in8(register_8_q), .in9(register_9_q),
    .in10(register_10_q), .in11(register_11_q), .in12(register_12_q), .in13(register_13_q),
    .in14(register_14_q), .in15(register_15_q), .in16(register_16_q), .in17(register_17_q),
    .in18(register_18_q), .in19(register_19_q), .in20(register_20_q), .in21(register_21_q),
    .in22(register_22_q), .in23(register_23_q), .in24(register_24_q), .in25(register_25_q),
    .in26(register_26_q), .in27(register_27_q), .in28(register_28_q), .in29(register_29_q),
    .in30(register_30_q), .in31(register_31_q), .out(Source_Register_2_2), .sel(Source_Register_2));
endmodule

module Control_Decoder (
  input  R_Type,
  input  I_Type_lw,
  input  I_Type_addi,
  input  I_Type_jalr,
  input  S_Type,
  input  SB_Type,
  input  U_Type_auipc,
  input  U_Type_lui,
  input  UJ_Type,
  input  func_7_6th_Bit__30th_Bit,
  input  [2:0] funct_3,
  output Write,
  output Store,
  output Load,
  output Branch,
  output [1:0] ALU_s_Operand_A,
  output ALU_s_Operand_B,
  output [1:0] ALU_s_Immediate,
  output [1:0] ALU_s_Next_PC,
  output [3:0] ALU_s_Operation_Selector
);

  wire alu_operation_selector_1_a, alu_operation_selector_1_b, alu_operation_selector_1_c;

  or or_1 (Write, R_Type, I_Type_lw, I_Type_addi, I_Type_jalr, U_Type_auipc, U_Type_lui, UJ_Type);
  Operand_A_Selector_in_ALU operand_a_selector_in_alu_1 (
    .R(R_Type), .lw(I_Type_lw), .addi(I_Type_addi), .jalr(I_Type_jalr), .S(S_Type), .SB(SB_Type),
    .auipcPC(U_Type_auipc), .jalr2(I_Type_jalr), .jal(UJ_Type), .zero(1'b0), .a(ALU_s_Operand_A[0]),
    .b(ALU_s_Operand_A[1]));
  Operand_B_Selector_in_ALU operand_b_selector_in_alu_1 (
    .I_Type_lw(I_Type_lw), .I_Type_addi(I_Type_addi), .I_Type_jalr(I_Type_jalr), .S_Type(S_Type),
    .U_Type_auipc(U_Type_auipc), .U_Type_lui(U_Type_lui), .X(ALU_s_Operand_B));
  Immediate_Selector_in_ALU immediate_selector_in_alu_1 (
    .I_lw(I_Type_lw), .I_addi(I_Type_addi), .I_jalr(I_Type_jalr), .S(S_Type), .U_auipc(U_Type_auipc),
    .U_lui(U_Type_lui), .a(ALU_s_Immediate[0]), .b(ALU_s_Immediate[1]));
  Next_PC_Selector next_pc_selector_1 (
    .jalr(SB_Type), .SB(I_Type_jalr), .jal(UJ_Type), .a(ALU_s_Next_PC[0]), .b(ALU_s_Next_PC[1]));
  ALU_Operation_Selector alu_operation_selector_1 (
    .R(R_Type), .I_lw(I_Type_lw), .I_addi(I_Type_addi), .I_jalr(I_Type_jalr), .S(S_Type),
    .U_auipc(U_Type_auipc), .U_lui(U_Type_lui), .UJ(UJ_Type), .a(alu_operation_selector_1_a),
    .b(alu_operation_selector_1_b), .c(alu_operation_selector_1_c));
  ALU_Controller alu_controller_1 (
    .ALU_Opcode_2nd_Bit(alu_operation_selector_1_c), .ALU_Opcode_1st_Bit(alu_operation_selector_1_b),
    .ALU_Opcode_0th_Bit(alu_operation_selector_1_a), .func_7_6th_Bit(func_7_6th_Bit__30th_Bit),
    .func_3_2nd_Bit(funct_3[2]), .func_3_1st_Bit(funct_3[1]), .func_3_0th_Bit(funct_3[0]),
    .a(ALU_s_Operation_Selector[3]), .b(ALU_s_Operation_Selector[2]), .c(ALU_s_Operation_Selector[1]),
    .d(ALU_s_Operation_Selector[0]));

  assign Branch = SB_Type;
  assign Load = I_Type_lw;
  assign Store = S_Type;
endmodule

module Operand_A_Selector_in_ALU (
  input  R,
  input  lw,
  input  addi,
  input  jalr,
  input  S,
  input  SB,
  input  auipcPC,
  input  jalr2,
  input  jal,
  input  zero,
  output a,
  output b
);

  or or_1 (a, zero, jal, jalr2, jalr);
  or or_2 (b, zero, auipcPC);
endmodule

module Operand_B_Selector_in_ALU (
  input  I_Type_lw,
  input  I_Type_addi,
  input  I_Type_jalr,
  input  S_Type,
  input  U_Type_auipc,
  input  U_Type_lui,
  output X
);

  or or_1 (X, U_Type_lui, U_Type_auipc, S_Type, I_Type_jalr, I_Type_addi, I_Type_lw);
endmodule

module Immediate_Selector_in_ALU (
  input  I_lw,
  input  I_addi,
  input  I_jalr,
  input  S,
  input  U_auipc,
  input  U_lui,
  output a,
  output b
);

  wire not_1_out, not_2_out, not_3_out, not_4_out, not_5_out, not_6_out, not_7_out, not_8_out, not_9_out;

  not not_1 (not_1_out, I_lw);
  not not_2 (not_2_out, I_addi);
  not not_3 (not_3_out, I_jalr);
  not not_4 (not_4_out, S);
  not not_5 (not_5_out, I_lw);
  not not_6 (not_6_out, I_addi);
  not not_7 (not_7_out, I_jalr);
  not not_8 (not_8_out, U_auipc);
  not not_9 (not_9_out, U_lui);
  and and_1 (a, not_1_out, not_2_out, not_3_out, not_4_out);
  and and_2 (b, not_5_out, not_6_out, not_7_out, not_8_out, not_9_out);
endmodule

module Next_PC_Selector (
  input  jalr,
  input  SB,
  input  jal,
  output a,
  output b
);

  or or_1 (a, jal, SB);
  or or_2 (b, jal, jalr);
endmodule

module ALU_Operation_Selector (
  input  R,
  input  I_lw,
  input  I_addi,
  input  I_jalr,
  input  S,
  input  U_auipc,
  input  U_lui,
  input  UJ,
  output a,
  output b,
  output c
);

  or or_1 (a, UJ, U_lui, U_auipc, S);
  or or_2 (b, UJ, U_lui, I_jalr, I_addi);
  or or_3 (c, UJ, U_auipc, I_jalr, I_lw);
endmodule

module ALU_Controller (
  input  ALU_Opcode_2nd_Bit,
  input  ALU_Opcode_1st_Bit,
  input  ALU_Opcode_0th_Bit,
  input  func_7_6th_Bit,
  input  func_3_2nd_Bit,
  input  func_3_1st_Bit,
  input  func_3_0th_Bit,
  output a,
  output b,
  output c,
  output d
);

  wire and_1_out, and_2_out, and_3_out, and_4_out, and_5_out, and_6_out, and_7_out, and_8_out, and_9_out,
       and_10_out, and_11_out, and_12_out, and_13_out, and_14_out, and_15_out, and_16_out, not_1_out,
       not_2_out, not_3_out, not_4_out, not_5_out, not_6_out, not_7_out, not_8_out, not_9_out, not_10_out,
       not_11_out, not_12_out, not_13_out, not_14_out, not_15_out, not_16_out, not_17_out, not_18_out,
       not_19_out, not_20_out, not_21_out, not_22_out, not_23_out, not_24_out, not_25_out, not_26_out,
       not_27_out, not_28_out, not_29_out, not_30_out, not_31_out;

  not not_1 (not_1_out, ALU_Opcode_2nd_Bit);
  not not_2 (not_2_out, func_3_2nd_Bit);
  not not_3 (not_3_out, ALU_Opcode_2nd_Bit);
  not not_4 (not_4_out, func_3_1st_Bit);
  not not_5 (not_5_out, ALU_Opcode_2nd_Bit);
  not not_6 (not_6_out, func_7_6th_Bit);
  not not_7 (not_7_out, func_3_1st_Bit);
  not not_8 (not_8_out, ALU_Opcode_2nd_Bit);
  not not_9 (not_9_out, ALU_Opcode_0th_Bit);
  not not_10 (not_10_out, func_3_2nd_Bit);
  not not_11 (not_11_out, func_3_0th_Bit);
  not not_12 (not_12_out, ALU_Opcode_2nd_Bit);
  not not_13 (not_13_out, func_3_1st_Bit);
  not not_14 (not_14_out, func_3_0th_Bit);
  not not_15 (not_15_out, ALU_Opcode_2nd_Bit);
  not not_16 (not_16_out, ALU_Opcode_0th_Bit);
  not not_17 (not_17_out, func_3_0th_Bit);
  not not_18 (not_18_out, ALU_Opcode_2nd_Bit);
  not not_19 (not_19_out, func_7_6th_Bit);
  not not_20 (not_20_out, ALU_Opcode_2nd_Bit);
  not not_21 (not_21_out, ALU_Opcode_2nd_Bit);
  not not_22 (not_22_out, func_3_2nd_Bit);
  not not_23 (not_23_out, func_3_1st_Bit);
  not not_24 (not_24_out, ALU_Opcode_2nd_Bit);
  not not_25 (not_25_out, ALU_Opcode_0th_Bit);
  not not_26 (not_26_out, func_3_0th_Bit);
  not not_27 (not_27_out, ALU_Opcode_1st_Bit);
  not not_28 (not_28_out, ALU_Opcode_0th_Bit);
  not not_29 (not_29_out, func_3_1st_Bit);
  not not_30 (not_30_out, ALU_Opcode_2nd_Bit);
  not not_31 (not_31_out, func_3_1st_Bit);
  and and_1 (and_1_out, not_1_out, not_2_out, func_3_1st_Bit, func_3_0th_Bit);
  and and_2 (and_2_out, not_3_out, func_7_6th_Bit, not_4_out, func_3_0th_Bit);
  and and_3 (and_3_out, ALU_Opcode_1st_Bit, ALU_Opcode_0th_Bit);
  and and_4 (and_4_out, not_5_out, not_6_out, not_7_out, func_3_0th_Bit);
  and and_5 (and_5_out, not_8_out, not_9_out, not_10_out, func_3_1st_Bit, not_11_out);
  and and_6 (and_6_out, not_12_out, func_3_2nd_Bit, not_13_out, not_14_out);
  and and_7 (and_7_out, ALU_Opcode_1st_Bit, ALU_Opcode_0th_Bit);
  and and_8 (and_8_out, not_15_out, not_16_out, func_3_1st_Bit, not_17_out);
  and and_9 (and_9_out, not_18_out, not_19_out, func_3_2nd_Bit, func_3_0th_Bit);
  and and_10 (and_10_out, not_20_out, func_3_2nd_Bit, func_3_1st_Bit);
  and and_11 (and_11_out, ALU_Opcode_1st_Bit, ALU_Opcode_0th_Bit);
  and and_12 (and_12_out, not_21_out, not_22_out, not_23_out, func_3_0th_Bit);
  and and_13 (and_13_out, not_24_out, not_25_out, func_3_1st_Bit, not_26_out);
  and and_14 (and_14_out, not_27_out, not_28_out, func_7_6th_Bit, not_29_out);
  and and_15 (and_15_out, not_30_out, func_7_6th_Bit, not_31_out, func_3_0th_Bit);
  and and_16 (and_16_out, ALU_Opcode_1st_Bit, ALU_Opcode_0th_Bit);
  or or_1 (a, and_1_out, and_2_out, and_3_out);
  or or_2 (b, and_4_out, and_5_out, and_6_out, and_7_out);
  or or_3 (c, and_8_out, and_9_out, and_10_out, and_11_out);
  or or_4 (d, and_12_out, and_13_out, and_14_out, and_15_out, and_16_out);
endmodule

module ALU (
  input  [3:0] Operation_Select,
  input  [31:0] Operand_A,
  input  [31:0] Operand_B,
  output [31:0] Data_Memory
);

  wire comparator_1_lt, comparator_2_lt;
  wire [31:0] adder_1_out, and_1_out, multiplexer_1_out, multiplexer_2_out, or_1_out, shifter_1_out,
       shifter_2_out, shifter_3_out, subtractor_1_out, xor_1_out;

  Adder #(.width(32)) adder_1 (.a(Operand_A), .b(Operand_B), .out(adder_1_out), .cin(1'b0));  // open: cout
  Subtractor #(.width(32)) subtractor_1 (
    .a(Operand_A), .b(Operand_B), .out(subtractor_1_out), .bin(1'b0));  // open: bout
  Shifter #(.width(32)) shifter_1 (.in(Operand_A), .\dist (Operand_B[4:0]), .out(shifter_1_out));
  Shifter #(.width(32), .shift("lr")) shifter_2 (.in(Operand_A), .\dist (Operand_B[4:0]), .out(shifter_2_out));
  Comparator #(.width(32)) comparator_1 (.a(Operand_A), .b(Operand_B), .lt(comparator_1_lt));  // open: gt, eq
  Comparator #(.width(32), .mode("unsigned")) comparator_2 (
    .a(Operand_A), .b(Operand_B), .lt(comparator_2_lt));  // open: gt, eq
  Shifter #(.width(32), .shift("ar")) shifter_3 (.in(Operand_A), .\dist (Operand_B[4:0]), .out(shifter_3_out));
  assign and_1_out = Operand_A & Operand_B;  // AND_Gate and_1, 32 bits wide
  assign or_1_out = Operand_A | Operand_B;  // OR_Gate or_1, 32 bits wide
  assign xor_1_out = Operand_A ^ Operand_B;  // XOR_Gate xor_1, 32 bits wide
  Multiplexer #(.width(32), .enable("false")) multiplexer_1 (
    .in0({32{1'b0}}), .in1(32'h1), .out(multiplexer_1_out), .sel(comparator_1_lt));
  Multiplexer #(.width(32), .enable("false")) multiplexer_2 (
    .in0({32{1'b0}}), .in1(32'h1), .out(multiplexer_2_out), .sel(comparator_2_lt));
  Multiplexer #(.select(4), .width(32), .enable("false")) multiplexer_3 (
    .in0(adder_1_out), .in1(subtractor_1_out), .in2(and_1_out), .in3(or_1_out), .in4(xor_1_out),
    .in5(shifter_1_out), .in6(shifter_2_out), .in7(multiplexer_1_out), .in8(multiplexer_2_out),
    .in9(shifter_3_out), .in15(Operand_B), .out(Data_Memory), .sel(Operation_Select));  // open: in10, in11, in12, in13, in14
endmodule

module Control_Unit (
  input  [6:0] Instruction_Memory,
  input  func_7,
  input  [2:0] func_3,
  output Write,
  output Store,
  output Load,
  output Branch,
  output [1:0] Operand_A,
  output Operand_B,
  output [1:0] Immediate_Selector,
  output [1:0] Next_PC,
  output [3:0] ALU_Operators
);

  wire type_decoder_1_i_type, type_decoder_1_i_type_2, type_decoder_1_i_type_3, type_decoder_1_r_type,
       type_decoder_1_s_type, type_decoder_1_sb_type, type_decoder_1_u_type, type_decoder_1_u_type_2,
       type_decoder_1_uj_type;

  Type_Decoder type_decoder_1 (
    .Instruction_Memory(Instruction_Memory), .R_Type(type_decoder_1_r_type), .I_Type(type_decoder_1_i_type),
    .I_Type_2(type_decoder_1_i_type_2), .I_Type_3(type_decoder_1_i_type_3), .S_Type(type_decoder_1_s_type),
    .SB_Type(type_decoder_1_sb_type), .U_Type(type_decoder_1_u_type), .U_Type_2(type_decoder_1_u_type_2),
    .UJ_Type(type_decoder_1_uj_type));
  Control_Decoder control_decoder_1 (
    .Write(Write), .Store(Store), .Load(Load), .Branch(Branch), .ALU_s_Operand_A(Operand_A),
    .ALU_s_Operand_B(Operand_B), .ALU_s_Immediate(Immediate_Selector), .ALU_s_Next_PC(Next_PC),
    .R_Type(type_decoder_1_r_type), .I_Type_lw(type_decoder_1_i_type), .I_Type_addi(type_decoder_1_i_type_2),
    .I_Type_jalr(type_decoder_1_i_type_3), .S_Type(type_decoder_1_s_type), .SB_Type(type_decoder_1_sb_type),
    .U_Type_auipc(type_decoder_1_u_type), .U_Type_lui(type_decoder_1_u_type_2),
    .UJ_Type(type_decoder_1_uj_type), .funct_3(func_3), .func_7_6th_Bit__30th_Bit(func_7),
    .ALU_s_Operation_Selector(ALU_Operators));
endmodule

module Branch_Selector (
  input  EN,
  input  [2:0] func_3,
  input  [31:0] rs1,
  input  [31:0] rs2,
  output O_P
);

  wire comparator_1_eq, comparator_2_eq, comparator_3_lt, comparator_4_eq, comparator_4_gt, comparator_5_lt,
       comparator_6_eq, comparator_6_gt, not_1_out, or_1_out, or_2_out;

  Comparator #(.width(32)) comparator_1 (.a(rs1), .b(rs2), .eq(comparator_1_eq));  // open: gt, lt
  Comparator #(.width(32)) comparator_2 (.a(rs1), .b(rs2), .eq(comparator_2_eq));  // open: gt, lt
  Comparator #(.width(32)) comparator_3 (.a(rs1), .b(rs2), .lt(comparator_3_lt));  // open: gt, eq
  Comparator #(.width(32)) comparator_4 (.a(rs1), .b(rs2), .gt(comparator_4_gt), .eq(comparator_4_eq));  // open: lt
  Comparator #(.width(32), .mode("unsigned")) comparator_5 (.a(rs1), .b(rs2), .lt(comparator_5_lt));  // open: gt, eq
  Comparator #(.width(32), .mode("unsigned")) comparator_6 (
    .a(rs1), .b(rs2), .gt(comparator_6_gt), .eq(comparator_6_eq));  // open: lt
  not not_1 (not_1_out, comparator_2_eq);
  or or_1 (or_1_out, comparator_4_gt, comparator_4_eq);
  or or_2 (or_2_out, comparator_6_gt, comparator_6_eq);
  Multiplexer #(.select(3)) multiplexer_1 (
    .in0(comparator_1_eq), .in1(not_1_out), .in4(comparator_3_lt), .in5(or_1_out), .in6(comparator_5_lt),
    .in7(or_2_out), .out(O_P), .sel(func_3), .en(EN));  // open: in2, in3
endmodule
